// Logisim project mips.circ as structural Verilog
module Processor (
);

  wire and_1_out, and_2_out, and_3_out, Clk_out, comparator_1_lt, comparator_2_lt, ctrle_1_out_2,
       ctrle_2_out_2, jaljr_1_o, jump_1_jump, Jump_EXMEM_q, ltz_gez_1_bgez, ltz_gez_1_bltz, move1_1_we2,
       multiplexer_13_out, multiplexer_15_out, multiplexer_16_out, not_1_out, or_1_out, registerfile_1_p3,
       sign_1_s, slt_1_out_3, stall_1_s, useb_1_x, we_1_we, WE_EXMEM_q, WE_IDEX_q;
  wire [1:0] pcsel_1_out_3;
  wire [3:0] eqa_1_out_4, HAZARD_CTRL_q, mips_alu_1_p4;
  wire [4:0] Dest_EXMEM_q, Dest_IDEX_q, multiplexer_4_out, multiplexer_6_out, multiplexer_9_out,
       multiplexer_11_out, multiplexer_18_out, registerfile_1_p4, Shamt_IDEX_q;
  wire [5:0] Func_IDEX_q, mipsprogramrom_1_p3, multiplexer_10_out, OpCode_EXMEM_q;
  wire [25:0] inst_IFID_q, Target_IDEX_q;
  wire [31:0] A_IDEX_q, adder_1_out, adder_2_out, B_EXMEM_q, B_IDEX_q, bit_extender_1_out,
       bit_extender_2_out, bit_extender_3_out, D_EXMEM_q, Imm_IDEX_q, memory_1_out_5, mips_alu_1_p3,
       mips_alu_1_p6, mipsprogramrom_1_p2, multiplexer_1_out, multiplexer_2_out, multiplexer_3_out,
       multiplexer_5_out, multiplexer_7_out, multiplexer_8_out, multiplexer_14_out, multiplexer_17_out,
       multiplexer_19_out, PC4_IDEX_q, PC4_q, plus4_1_out_2, registerfile_1_p1, registerfile_1_p7,
       registerfile_1_p8, shifter_1_out, subtractor_1_out;
  wire [31:5] multiplexer_11_out_2;
  wire [31:26] inst_IFID_q_2;

  Clock Clk (.out(Clk_out));
  Plus4 plus4_1 (.in_1(multiplexer_1_out), .out_2(plus4_1_out_2));
  Multiplexer #(.width(32), .enable("false")) multiplexer_1 (
    .in0(PC4_q), .in1(subtractor_1_out), .out(multiplexer_1_out), .sel(stall_1_s));
  Multiplexer #(.select(2), .width(32), .enable("false")) multiplexer_2 (
    .in0(plus4_1_out_2), .in1({multiplexer_11_out_2, multiplexer_11_out}), .in2(adder_1_out),
    .in3({PC4_IDEX_q[31:28], Target_IDEX_q, 2'b00}), .out(multiplexer_2_out), .sel(pcsel_1_out_3));
  Register #(.width(32)) inst_IFID (
    .D(mipsprogramrom_1_p2), .clk(Clk_out), .Q({inst_IFID_q_2, inst_IFID_q}));  // open: en, clr
  Register #(.width(32)) PC4 (.D(multiplexer_2_out), .clk(Clk_out), .Q(PC4_q));  // open: en, clr
  Subtractor #(.width(32)) subtractor_1 (.a(PC4_q), .b(32'h4), .out(subtractor_1_out));  // open: bin, bout
  // MIPSProgramROM mipsprogramrom_1: pin names not known; wires that end beside it: multiplexer_1_out, mipsprogramrom_1_p2, mipsprogramrom_1_p3
  Stall stall_1 (.dop(mipsprogramrom_1_p3), .eq(or_1_out), .s(stall_1_s));
  or or_1 (or_1_out, eqa_1_out_4[2], eqa_1_out_4[0]);
  WE we_1 (.j(Jump_EXMEM_q), .in_2(inst_IFID_q_2), .s(stall_1_s), .WE(we_1_we));
  // RegisterFile #(.trigger("falling")) registerfile_1: pin names not known; wires that end beside it: registerfile_1_p1, Clk_out, registerfile_1_p3, registerfile_1_p4, inst_IFID_q[25:21], inst_IFID_q[20:16], registerfile_1_p7, registerfile_1_p8
  useb useb_1 (.in_1(inst_IFID_q_2), .x(useb_1_x));
  assign bit_extender_1_out = {{16{inst_IFID_q[15]}}, inst_IFID_q[15:0]};  // Bit_Extender bit_extender_1
  assign bit_extender_2_out = {{16{1'b0}}, inst_IFID_q[15:0]};  // Bit_Extender bit_extender_2
  ctrle ctrle_1 (.in_1(inst_IFID_q_2), .out_2(ctrle_1_out_2));
  Multiplexer #(.width(32), .enable("false")) multiplexer_3 (
    .in0(bit_extender_1_out), .in1(bit_extender_2_out), .out(multiplexer_3_out), .sel(sign_1_s));
  sign sign_1 (.in_1(inst_IFID_q_2), .s(sign_1_s));
  Multiplexer #(.width(5), .enable("false")) multiplexer_4 (
    .in0(inst_IFID_q[20:16]), .in1(inst_IFID_q[15:11]), .out(multiplexer_4_out), .sel(ctrle_1_out_2));
  EqA eqa_1 (.r(inst_IFID_q[25:21]), .d(multiplexer_18_out), .w(move1_1_we2), .out_4(eqa_1_out_4[0]));
  EqA eqa_2 (.r(inst_IFID_q[25:21]), .d(Dest_EXMEM_q), .w(WE_EXMEM_q), .out_4(eqa_1_out_4[1]));
  EqB eqb_1 (.r(inst_IFID_q[20:16]), .d(multiplexer_18_out), .w(move1_1_we2), .t(useb_1_x), .out_5(eqa_1_out_4[2]));
  EqB eqb_2 (.r(inst_IFID_q[20:16]), .d(Dest_EXMEM_q), .w(WE_EXMEM_q), .t(useb_1_x), .out_5(eqa_1_out_4[3]));
  Register #(.width(1)) WE_IDEX (.D(we_1_we), .clk(Clk_out), .Q(WE_IDEX_q));  // open: en, clr
  Register #(.width(4)) HAZARD_CTRL (.D(eqa_1_out_4), .clk(Clk_out), .Q(HAZARD_CTRL_q));  // open: en, clr
  Register #(.width(32)) A_IDEX (.D(registerfile_1_p7), .clk(Clk_out), .Q(A_IDEX_q));  // open: en, clr
  Register #(.width(32)) B_IDEX (.D(registerfile_1_p8), .clk(Clk_out), .Q(B_IDEX_q));  // open: en, clr
  Register #(.width(32)) Imm_IDEX (.D(multiplexer_3_out), .clk(Clk_out), .Q(Imm_IDEX_q));  // open: en, clr
  Register #(.width(5)) Dest_IDEX (.D(multiplexer_4_out), .clk(Clk_out), .Q(Dest_IDEX_q));  // open: en, clr
  Register #(.width(5)) Shamt_IDEX (.D(inst_IFID_q[10:6]), .clk(Clk_out), .Q(Shamt_IDEX_q));  // open: en, clr
  Register #(.width(6)) Func_IDEX (.D(inst_IFID_q[5:0]), .clk(Clk_out), .Q(Func_IDEX_q));  // open: en, clr
  Register #(.width(6)) OpCode_IDEX (.D(inst_IFID_q_2), .clk(Clk_out), .Q(mipsprogramrom_1_p3));  // open: en, clr
  Register #(.width(32)) PC4_IDEX (.D(PC4_q), .clk(Clk_out), .Q(PC4_IDEX_q));  // open: en, clr
  Register #(.width(26)) Target_IDEX (.D(inst_IFID_q), .clk(Clk_out), .Q(Target_IDEX_q));  // open: en, clr
  Multiplexer #(.width(32), .enable("false")) multiplexer_5 (
    .in0(Imm_IDEX_q), .in1(B_IDEX_q), .out(multiplexer_5_out), .sel(ctrle_2_out_2));
  Multiplexer #(.width(5), .enable("false")) multiplexer_6 (
    .in0(Shamt_IDEX_q), .in1(multiplexer_11_out), .out(multiplexer_6_out), .sel(Func_IDEX_q[2]));
  and and_1 (and_1_out, HAZARD_CTRL_q[1], ~HAZARD_CTRL_q[0]);  // AND_Gate
  Multiplexer #(.width(32), .enable("false")) multiplexer_7 (
    .in0(A_IDEX_q), .in1(memory_1_out_5), .out(multiplexer_7_out), .sel(HAZARD_CTRL_q[0]));
  and and_2 (and_2_out, HAZARD_CTRL_q[3], ~HAZARD_CTRL_q[2]);  // AND_Gate
  Multiplexer #(.width(32), .enable("false")) multiplexer_8 (
    .in0(multiplexer_5_out), .in1(memory_1_out_5), .out(multiplexer_8_out), .sel(HAZARD_CTRL_q[2]));
  ctrle ctrle_2 (.in_1(mipsprogramrom_1_p3), .out_2(ctrle_2_out_2));
  Multiplexer #(.width(5), .enable("false")) multiplexer_9 (
    .in0(5'b10000), .in1(multiplexer_6_out), .out(multiplexer_9_out), .sel(ctrle_2_out_2));
  Multiplexer #(.width(6), .enable("false")) multiplexer_10 (
    .in0(mipsprogramrom_1_p3), .in1(Func_IDEX_q), .out(multiplexer_10_out), .sel(ctrle_2_out_2));
  Multiplexer #(.width(32), .enable("false")) multiplexer_11 (
    .in0(multiplexer_7_out), .in1(registerfile_1_p1), .out({multiplexer_11_out_2, multiplexer_11_out}),
    .sel(and_1_out));
  // Mips_ALU mips_alu_1: pin names not known; wires that end beside it: mipsprogramrom_1_p3, {multiplexer_11_out_2, multiplexer_11_out}, mips_alu_1_p3, mips_alu_1_p4, multiplexer_9_out, mips_alu_1_p6
  Multiplexer #(.width(32), .enable("false")) multiplexer_12 (
    .in0(multiplexer_8_out), .in1(registerfile_1_p1), .out(mips_alu_1_p3), .sel(and_2_out));
  ALUop aluop_1 (.in_1(multiplexer_10_out), .out_2(mips_alu_1_p4));
  Shifter #(.width(32)) shifter_1 (.in(Imm_IDEX_q), .\dist (5'b00010), .out(shifter_1_out));
  Adder #(.width(32)) adder_1 (.a(shifter_1_out), .b(PC4_IDEX_q), .out(adder_1_out));  // open: cin, cout
  Comparator #(.width(32)) comparator_1 (
    .a({multiplexer_11_out_2, multiplexer_11_out}), .b(mips_alu_1_p3), .lt(comparator_1_lt));  // open: gt, eq
  Comparator #(.width(32), .mode("unsigned")) comparator_2 (
    .a({multiplexer_11_out_2, multiplexer_11_out}), .b(mips_alu_1_p3), .lt(comparator_2_lt));  // open: gt, eq
  slt slt_1 (.in_1(Func_IDEX_q), .o(ctrle_2_out_2), .out_3(slt_1_out_3));
  jaljr jaljr_1 (.in_1(Func_IDEX_q), .in_2(ctrle_2_out_2), .o(jaljr_1_o));
  not not_1 (not_1_out, Func_IDEX_q[5]);
  Multiplexer #(.enable("false")) multiplexer_13 (
    .in0(comparator_1_lt), .in1(comparator_2_lt), .out(multiplexer_13_out), .sel(multiplexer_10_out[0]));
  and and_3 (and_3_out, not_1_out, ctrle_2_out_2);
  assign bit_extender_3_out = {{31{1'b0}}, multiplexer_13_out};  // Bit_Extender bit_extender_3
  Adder #(.width(32)) adder_2 (.a(32'h8), .b(PC4_IDEX_q), .out(adder_2_out));  // open: cin, cout
  Multiplexer #(.width(32), .enable("false")) multiplexer_14 (
    .in0(bit_extender_3_out), .in1({multiplexer_11_out_2, multiplexer_11_out}), .out(multiplexer_14_out),
    .sel(and_3_out));
  ltz_gez ltz_gez_1 (.in_1(mips_alu_1_p6), .lez(mips_alu_1_p6[0]), .bgez(ltz_gez_1_bgez), .bltz(ltz_gez_1_bltz));
  Multiplexer #(.enable("false")) multiplexer_15 (
    .in0(ltz_gez_1_bltz), .in1(ltz_gez_1_bgez), .out(multiplexer_15_out), .sel(Dest_IDEX_q[0]));
  Multiplexer #(.enable("false")) multiplexer_16 (
    .in0(multiplexer_15_out), .in1(mips_alu_1_p6[0]), .out(multiplexer_16_out), .sel(mipsprogramrom_1_p3[2]));
  Multiplexer #(.width(32), .enable("false")) multiplexer_17 (
    .in0(mips_alu_1_p6), .in1(multiplexer_14_out), .out(multiplexer_17_out), .sel(slt_1_out_3));
  Multiplexer #(.width(5), .enable("false")) multiplexer_18 (
    .in0(Dest_IDEX_q), .in1({5{1'b1}}), .out(multiplexer_18_out), .sel(jaljr_1_o));
  Register #(.width(1)) WE_EXMEM (.D(move1_1_we2), .clk(Clk_out), .Q(WE_EXMEM_q));  // open: en, clr
  Move1 move1_1 (.we(WE_IDEX_q), .ctrl(ctrle_2_out_2), .func(Func_IDEX_q), .Be(mips_alu_1_p3[0]), .we2(move1_1_we2));
  Register #(.width(32)) D_EXMEM (.D(multiplexer_19_out), .clk(Clk_out), .Q(D_EXMEM_q));  // open: en, clr
  Multiplexer #(.width(32), .enable("false")) multiplexer_19 (
    .in0(multiplexer_17_out), .in1(adder_2_out), .out(multiplexer_19_out), .sel(jaljr_1_o));
  Register #(.width(32)) B_EXMEM (.D(B_IDEX_q), .clk(Clk_out), .Q(B_EXMEM_q));  // open: en, clr
  Register #(.width(5)) Dest_EXMEM (.D(multiplexer_18_out), .clk(Clk_out), .Q(Dest_EXMEM_q));  // open: en, clr
  Register #(.width(1)) Jump_EXMEM (.D(jump_1_jump), .clk(Clk_out), .Q(Jump_EXMEM_q));  // open: en, clr
  Jump jump_1 (.bra(multiplexer_16_out), .jal(jaljr_1_o), .op(mipsprogramrom_1_p3), .jump(jump_1_jump));
  Register #(.width(6)) OpCode_EXMEM (.D(mipsprogramrom_1_p3), .clk(Clk_out), .Q(OpCode_EXMEM_q));  // open: en, clr
  PCsel pcsel_1 (.jump(jump_1_jump), .op(mipsprogramrom_1_p3), .out_3(pcsel_1_out_3));
  Memory memory_1 (.D(D_EXMEM_q), .B(B_EXMEM_q), .op(OpCode_EXMEM_q), .clk(Clk_out), .out_5(memory_1_out_5));
  Register #(.width(32)) D_MEMWB (.D(memory_1_out_5), .clk(Clk_out), .Q(registerfile_1_p1));  // open: en, clr
  Register #(.width(5)) Dest_MEMWB (.D(Dest_EXMEM_q), .clk(Clk_out), .Q(registerfile_1_p4));  // open: en, clr
  Register #(.width(1)) WE_MEMWB (.D(WE_EXMEM_q), .clk(Clk_out), .Q(registerfile_1_p3));  // open: en, clr

  // Notes on the sheet:
  //   contents of mipsprogramrom_1 (hex, n*v repeats v):
  //   BLEZ $23, PROCEED SLL $0,$0, 0 #delay slot SLL $0,$0, 0 #filler code  J TESTJALR SLL $0,$0, 0 #delay
  //   slot SLL $0,$0, 0 #filler code  PROCEED: JR $31 SLL $0,$0, 0 #delay slot SLL $0,$0, 0 #filler code
  //   #Jumptest should not be executed JUMPTEST:  #BNE $12, $0, JRPASSED SLL $0,$0, 0 #delay slot SLL
  //   $0,$0, 0 #filler code  #BLTZ $12, JPASSED SLL $0,$0, 0 #delay slot SLL $0,$0, 0 #filler code  #BEQ
  //   $12, $0, TESTJALR SLL $0,$0, 0 #delay slot SLL $0,$0, 0 #filler code  START:  ADDIU $1,$0,31
  //   #$1=0x000fffff   ADDIU $2,$0,31  #$2=0x000fffff  #$19 = Branch Taken #$20 = Branch taken delay slot
  //   #$21 = Branch not taken #$22 = No WB if Branch taken (should stay 0) #$23 = random numbers from
  //   filler code #$30 = low number comparison branch #$31 = High number comparison branch  ADDIU
  //   $31,$31,32700  #0x4C4B40 ADDIU $30, $30, -32700 #  #Testing BEQ #sucess BEQ BEQ $1,$2,ONE  ADDIU
  //   $20, $20, 1 #delay slot should be 1 ADDIU $22, $22, 1  #should be 0 SLL $0,$0, 0 #filler code SLL
  //   $0,$0, 0 #filler code  ONE: ADDIU $19,$19,1 #19 should be 1 because branch taken  #Fail BEQ BEQ $1,
  //   $30, TWO ADDIU $23, $23, 15 SLL $0,$0, 0 #filler code SLL $0,$0, 0 #filler code ADDIU $23, $23, 15
  //   TWO: ADDIU $21,$21,1   #21 should be 1 because branch not taken  #Testing BNE BNE $1,$31, THREE
  //   ADDIU $20, $20, 1 #delay slot should be 2 ADDIU $22, $0, 1  #should be 0 SLL $0,$0, 0 #filler code
  //   SLL $0,$0, 0 #filler code  THREE: ADDIU $19,$19,1 #19 should be 2 because branch taken  #Fail BNE
  //   BNE $1,$2, FOUR ADDIU $23, $23, 15 SLL $0,$0, 0 #filler code SLL $0,$0, 0 #filler code SLL $0,$0, 0
  //   #filler code ADDIU $23, $23, 15  FOUR: ADDIU $21,$21,1   #21 should be 2 because branch not taken
  //   #note BLEZ has 3 conditions to branch rather than 2  #Testing BLEZ for ==0 BLEZ $0, FIVE ADDIU $20,
  //   $20, 1 #delay slot should be 3 ADDIU $22, $22, 1  #should be 0 SLL $0,$0, 0 #filler code SLL $0,$0,
  //   0 #filler code  FIVE: ADDIU $19,$19,1 #19 should be 3 because branch taken  #Test where <0 pass BLEZ
  //   $30, SIX ADDIU $20, $20, 1 #delay slot should be 4 ADDIU $22, $22, 1  #should be 0 SLL $0,$0, 0
  //   #filler code SLL $0,$0, 0 #filler code SLL $0,$0, 0 #filler code SLL $0,$0, 0 #filler code  SIX:
  //   ADDIU $19,$19,1 #19 should be 4 because branch taken  #Fail BLEZ BLEZ $4, SEVEN ADDIU $23, $23, 15
  //   SLL $0,$0, 0 #filler code SLL $0,$0, 0 #filler code SLL $0,$0, 0 #filler code ADDIU $23, $23, 15
  //   SEVEN: ADDIU $21,$21,1   #21 should be 3 because branch not taken  #Testing BGTZ : pass BGTZ $1,
  //   EIGHT ADDIU $20, $20, 1 #delay slot should be 5 ADDIU $22, $22, 1 #should be 0 SLL $0,$0, 0 #filler
  //   code SLL $0,$0, 0 #filler code SLL $0,$0, 0 #filler code SLL $0,$0, 0 #filler code  EIGHT: ADDIU
  //   $19,$19,1 #19 should be 5 because branch taken  #Fail BGTZ BGTZ $0, NINE ADDIU $23, $23, 15 SLL
  //   $0,$0, 0 #filler code SLL $0,$0, 0 #filler code SLL $0,$0, 0 #filler code ADDIU $23, $23, 15  NINE:
  //   ADDIU $21,$21,1   #21 should be 4 because branch not taken  #Testing BLTZ : Pass BLTZ $30, ELEVEN
  //   ADDIU $20, $20, 1 #delay slot should be 6 ADDIU $22, $22, 1 #should be 0 SLL $0,$0, 0 #filler code
  //   SLL $0,$0, 0 #filler code SLL $0,$0, 0 #filler code SLL $0,$0, 0 #filler code  ELEVEN: ADDIU
  //   $19,$19,1 #19 should be 6 because branch taken  #Fail BLTZ BLTZ $0, TWELVE  ADDIU $23, $23, 15 SLL
  //   $0,$0, 0 #filler code SLL $0,$0, 0 #filler code SLL $0,$0, 0 #filler code ADDIU $23, $23, 15
  //   TWELVE: ADDIU $21,$21,1   #21 should be 5 because branch not taken  #note BGEZ has 3 possible branch
  //   conditions  #Testing BGEZ: Pass BGEZ $0, THIRTEEN ADDIU $20, $20, 1 #delay slot should be 7 ADDIU
  //   $22, $22, 1 #should be 0 SLL $0,$0, 0 #filler code SLL $0,$0, 0 #filler code SLL $0,$0, 0 #filler
  //   code SLL $0,$0, 0 #filler code  THIRTEEN: ADDIU $19,$19,1 #19 should be 7 because branch taken
  //   #Testing BGEZ: Pass BGEZ $31, FOURTEEN ADDIU $20, $20, 1 #delay slot should be 8 ADDIU $22, $22, 1
  //   #should be 0 SLL $0,$0, 0 #filler code SLL $0,$0, 0 #filler code SLL $0,$0, 0 #filler code SLL
  //   $0,$0, 0 #filler code  FOURTEEN: ADDIU $19,$19,1 #19 should be 8 because branch tak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
  //   branch
endmodule

module Memory (
  input  [31:0] D,
  input  [31:0] B,
  input  [5:0] op,
  input  clk,
  output [31:0] out_5
);

  wire and_1_out, ldst_1_ld, ldst_1_st, nor_1_out;
  wire [2:0] bit_extender_1_out;
  wire [3:0] multiplexer_1_out;
  wire [7:0] mips_ram_1_p7;
  wire [19:0] shifter_1_out;
  wire [31:0] bit_extender_2_out, bit_extender_3_out, multiplexer_2_out, multiplexer_3_out;
  wire [31:8] mips_ram_1_p7_2;

  Multiplexer #(.width(4), .enable("false")) multiplexer_1 (
    .in0(4'b0001), .in1(4'b1111), .out(multiplexer_1_out), .sel(op[0]));
  assign bit_extender_1_out = {{2{1'b0}}, op[4]};  // Bit_Extender bit_extender_1
  nor nor_1 (nor_1_out, D[20], D[21], D[22], D[23], D[24], D[25], D[26], D[27], D[28], D[29], D[30], D[31]);
  Shifter #(.width(20), .shift("ar")) shifter_1 (
    .in(D[19:0]), .\dist ({bit_extender_1_out, op[5:4]}), .out(shifter_1_out));
  ldst ldst_1 (.op5(op[5]), .a(op[4]), .b(op[3]), .c(op[2]), .d(op[1]), .op0(op[0]), .ld(ldst_1_ld), .st(ldst_1_st));
  and and_1 (and_1_out, nor_1_out, ldst_1_st);
  // MIPS_RAM mips_ram_1: pin names not known; wires that end beside it: shifter_1_out, B, and_1_out, multiplexer_1_out, clk, ldst_1_ld, {mips_ram_1_p7_2, mips_ram_1_p7}
  assign bit_extender_2_out = {{24{mips_ram_1_p7[7]}}, mips_ram_1_p7};  // Bit_Extender bit_extender_2
  assign bit_extender_3_out = {{24{1'b0}}, mips_ram_1_p7};  // Bit_Extender bit_extender_3
  Multiplexer #(.width(32), .enable("false")) multiplexer_2 (
    .in0(bit_extender_2_out), .in1(bit_extender_3_out), .out(multiplexer_2_out), .sel(op[2]));
  Multiplexer #(.width(32), .enable("false")) multiplexer_3 (
    .in0(multiplexer_2_out), .in1({mips_ram_1_p7_2, mips_ram_1_p7}), .out(multiplexer_3_out), .sel(op[0]));
  Multiplexer #(.width(32), .enable("false")) multiplexer_4 (
    .in0(D), .in1(multiplexer_3_out), .out(out_5), .sel(op[5]));
endmodule

module Plus4 (
  input  [31:0] in_1,
  output [31:0] out_2
);

  // Incrementer #(.width(30)) incrementer_1: pin names not known; wires that end beside it: in_1[31:2], out_2[31:2]

  assign out_2[1:0] = in_1[1:0];
endmodule

module useb (
  input  [5:0] in_1,
  output x
);

  wire and_1_out, and_2_out, ldst_1_ld, ldst_1_st, not_1_out, not_2_out, not_3_out, not_4_out, not_5_out,
       not_6_out, not_7_out, or_1_out, or_2_out;

  ldst ldst_1 (
    .op5(in_1[5]), .a(in_1[4]), .b(in_1[3]), .c(in_1[2]), .d(in_1[1]), .op0(in_1[0]), .ld(ldst_1_ld),
    .st(ldst_1_st));
  not not_1 (not_1_out, in_1[5]);
  not not_2 (not_2_out, in_1[4]);
  not not_3 (not_3_out, in_1[3]);
  not not_4 (not_4_out, in_1[1]);
  not not_5 (not_5_out, in_1[5]);
  not not_6 (not_6_out, in_1[4]);
  not not_7 (not_7_out, in_1[3]);
  and and_1 (and_1_out, not_1_out, not_2_out, not_3_out, not_4_out);
  and and_2 (and_2_out, not_5_out, not_6_out, not_7_out, in_1[2]);
  or or_1 (or_1_out, and_1_out, and_2_out);
  or or_2 (or_2_out, ldst_1_ld, ldst_1_st);
  or or_3 (x, or_1_out, or_2_out);
endmodule

module Move (
  input  we,
  input  i,
  input  ctrl,
  input  ff,
  input  Be,
  output we_2
);

  wire and_1_out, and_2_out, and_3_out, and_4_out, not_1_out, not_2_out, not_3_out, not_4_out;

  not not_1 (not_1_out, i);
  not not_2 (not_2_out, ctrl);
  not not_3 (not_3_out, ff);
  not not_4 (not_4_out, Be);
  and and_1 (and_1_out, we, not_1_out);
  and and_2 (and_2_out, we, not_2_out);
  and and_3 (and_3_out, we, not_3_out, not_4_out);
  and and_4 (and_4_out, we, ff, Be);
  or or_1 (we_2, and_1_out, and_2_out, and_3_out, and_4_out);
endmodule

module EqA (
  input  [4:0] r,
  input  [4:0] d,
  input  w,
  output out_4
);

  wire and_1_out, and_2_out, not_1_out, not_2_out, not_3_out, not_4_out, not_5_out, not_6_out;
  wire [4:0] xnor_1_out;

  assign xnor_1_out = ~(r ^ d);  // XNOR_Gate xnor_1, 5 bits wide
  not not_1 (not_1_out, d[0]);
  not not_2 (not_2_out, d[1]);
  not not_3 (not_3_out, d[2]);
  not not_4 (not_4_out, d[3]);
  not not_5 (not_5_out, d[4]);
  and and_1 (and_1_out, not_1_out, not_2_out, not_3_out, not_4_out, not_5_out);
  and and_2 (and_2_out, xnor_1_out[0], xnor_1_out[1], xnor_1_out[2], xnor_1_out[3], xnor_1_out[4]);
  not not_6 (not_6_out, and_1_out);
  and and_3 (out_4, not_6_out, and_2_out, w);
endmodule

module ALUop (
  input  [5:0] in_1,
  output [3:0] out_2
);

  wire and_1_out, and_2_out, and_3_out, and_4_out, and_5_out, and_6_out, and_7_out, and_8_out, and_9_out,
       and_10_out, and_11_out, and_12_out, and_13_out, and_14_out, and_15_out, and_16_out, and_17_out,
       and_18_out, and_19_out, and_20_out, and_21_out, and_22_out, and_23_out, and_24_out, not_1_out,
       not_2_out, not_3_out, not_4_out, not_5_out, not_6_out, not_7_out, not_8_out, not_9_out, not_10_out,
       not_11_out, not_12_out, not_13_out, not_14_out, not_15_out, not_16_out, not_17_out, not_18_out,
       not_19_out, not_20_out, not_21_out, not_22_out, not_23_out, not_24_out, not_25_out, not_26_out,
       not_27_out, not_28_out, not_29_out, not_30_out, not_31_out, not_32_out, not_33_out, not_34_out,
       not_35_out, not_36_out, not_37_out, not_38_out;

  not not_1 (not_1_out, in_1[5]);
  not not_2 (not_2_out, in_1[4]);
  not not_3 (not_3_out, in_1[3]);
  not not_4 (not_4_out, in_1[1]);
  not not_5 (not_5_out, in_1[5]);
  not not_6 (not_6_out, in_1[4]);
  not not_7 (not_7_out, in_1[3]);
  not not_8 (not_8_out, in_1[5]);
  not not_9 (not_9_out, in_1[0]);
  not not_10 (not_10_out, in_1[1]);
  not not_11 (not_11_out, in_1[0]);
  not not_12 (not_12_out, in_1[5]);
  not not_13 (not_13_out, in_1[4]);
  not not_14 (not_14_out, in_1[3]);
  not not_15 (not_15_out, in_1[2]);
  not not_16 (not_16_out, in_1[5]);
  not not_17 (not_17_out, in_1[0]);
  not not_18 (not_18_out, in_1[3]);
  not not_19 (not_19_out, in_1[0]);
  not not_20 (not_20_out, in_1[3]);
  not not_21 (not_21_out, in_1[0]);
  not not_22 (not_22_out, in_1[1]);
  not not_23 (not_23_out, in_1[5]);
  not not_24 (not_24_out, in_1[4]);
  not not_25 (not_25_out, in_1[3]);
  not not_26 (not_26_out, in_1[0]);
  not not_27 (not_27_out, in_1[2]);
  not not_28 (not_28_out, in_1[0]);
  not not_29 (not_29_out, in_1[0]);
  not not_30 (not_30_out, in_1[4]);
  not not_31 (not_31_out, in_1[3]);
  not not_32 (not_32_out, in_1[1]);
  not not_33 (not_33_out, in_1[2]);
  not not_34 (not_34_out, in_1[5]);
  not not_35 (not_35_out, in_1[3]);
  not not_36 (not_36_out, in_1[5]);
  not not_37 (not_37_out, in_1[4]);
  not not_38 (not_38_out, in_1[3]);
  and and_1 (and_1_out, not_1_out, not_2_out, not_3_out, not_4_out, in_1[0]);
  and and_2 (and_2_out, not_5_out, not_6_out, not_7_out, in_1[2]);
  and and_3 (and_3_out, not_8_out, in_1[3], not_9_out);
  and and_4 (and_4_out, in_1[3], in_1[2], not_10_out);
  and and_5 (and_5_out, in_1[4], in_1[3], not_11_out);
  and and_6 (and_6_out, in_1[5], in_1[2], in_1[1]);
  and and_7 (and_7_out, in_1[5], in_1[4], in_1[2]);
  and and_8 (and_8_out, not_12_out, not_13_out, not_14_out, not_15_out, in_1[0]);
  and and_9 (and_9_out, not_16_out, in_1[1], not_17_out);
  and and_10 (and_10_out, not_18_out, in_1[2], in_1[1]);
  and and_11 (and_11_out, in_1[2], in_1[1], not_19_out);
  and and_12 (and_12_out, in_1[4], not_20_out, in_1[1]);
  and and_13 (and_13_out, in_1[4], in_1[1], not_21_out);
  and and_14 (and_14_out, not_22_out, in_1[0]);
  and and_15 (and_15_out, not_23_out, not_24_out, not_25_out, in_1[2], in_1[1], not_26_out);
  and and_16 (and_16_out, in_1[3], not_27_out, in_1[1], not_28_out);
  and and_17 (and_17_out, in_1[4], in_1[3], in_1[1], not_29_out);
  and and_18 (and_18_out, in_1[5], not_30_out, not_31_out, not_32_out);
  and and_19 (and_19_out, in_1[5], not_33_out);
  and and_20 (and_20_out, in_1[5], in_1[0]);
  and and_21 (and_21_out, in_1[5], in_1[3], in_1[1]);
  and and_22 (and_22_out, in_1[5], in_1[4], in_1[1]);
  and and_23 (and_23_out, not_34_out, not_35_out, in_1[0]);
  or or_1 (out_2[0], and_23_out, and_24_out);
  and and_24 (and_24_out, not_36_out, not_37_out, not_38_out, in_1[2]);
  or or_2 (out_2[3], and_1_out, and_2_out, and_3_out, and_4_out, and_5_out, and_6_out, and_7_out);
  or or_3 (out_2[2], and_8_out, and_9_out, and_10_out, and_11_out, and_12_out, and_13_out);
  or or_4 (out_2[1], and_14_out, and_15_out, and_16_out, and_17_out, and_18_out, and_19_out, and_20_out, and_21_out, and_22_out);
endmodule

module WE (
  input  j,
  input  [5:0] in_2,
  input  s,
  output WE
);

  wire and_1_out, and_2_out, and_3_out, and_4_out, and_5_out, and_6_out, not_1_out, not_2_out, not_3_out,
       not_4_out, not_5_out, not_6_out, not_7_out, not_8_out, not_9_out, not_10_out, not_11_out, not_12_out,
       not_13_out, not_14_out, not_15_out, not_16_out, not_17_out, not_18_out, or_1_out;

  not not_1 (not_1_out, in_2[4]);
  not not_2 (not_2_out, in_2[3]);
  not not_3 (not_3_out, in_2[2]);
  not not_4 (not_4_out, in_2[1]);
  not not_5 (not_5_out, in_2[0]);
  not not_6 (not_6_out, in_2[5]);
  not not_7 (not_7_out, in_2[4]);
  not not_8 (not_8_out, in_2[5]);
  not not_9 (not_9_out, in_2[4]);
  not not_10 (not_10_out, in_2[5]);
  not not_11 (not_11_out, in_2[4]);
  not not_12 (not_12_out, in_2[4]);
  not not_13 (not_13_out, in_2[3]);
  not not_14 (not_14_out, in_2[1]);
  not not_15 (not_15_out, in_2[0]);
  not not_16 (not_16_out, in_2[4]);
  not not_17 (not_17_out, in_2[3]);
  not not_18 (not_18_out, in_2[2]);
  and and_1 (and_1_out, not_1_out, not_2_out, not_3_out, not_4_out, not_5_out);
  and and_2 (and_2_out, not_6_out, not_7_out, in_2[3], in_2[0]);
  and and_3 (and_3_out, not_8_out, not_9_out, in_2[3], in_2[1]);
  and and_4 (and_4_out, not_10_out, not_11_out, in_2[3], in_2[2]);
  and and_5 (and_5_out, in_2[5], not_12_out, not_13_out, not_14_out, not_15_out);
  and and_6 (and_6_out, in_2[5], not_16_out, not_17_out, not_18_out, in_2[1], in_2[0]);
  or or_1 (or_1_out, and_1_out, and_2_out, and_3_out, and_4_out, and_5_out, and_6_out);
  and and_7 (WE, or_1_out, ~j, ~s);  // AND_Gate
endmodule

module LUI (
  input  [5:0] LUI,
  input  [5:0] in_2,
  output out_3
);

  wire and_1_out, and_2_out, not_1_out, not_2_out, not_3_out, not_4_out;

  not not_1 (not_1_out, LUI[5]);
  not not_2 (not_2_out, LUI[4]);
  not not_3 (not_3_out, in_2[5]);
  not not_4 (not_4_out, in_2[4]);
  and and_1 (and_1_out, not_3_out, not_4_out, in_2[3], in_2[2], in_2[1], in_2[0]);
  and and_2 (and_2_out, not_1_out, not_2_out, LUI[3], LUI[2], LUI[1], LUI[0]);
  and and_3 (out_3, and_2_out, and_1_out);
endmodule

module Move1 (
  input  we,
  input  ctrl,
  input  [5:0] func,
  input  Be,
  output we2
);

  wire and_1_out, and_2_out, and_3_out, and_4_out, and_5_out, and_6_out, and_7_out, and_8_out, not_1_out,
       not_2_out, not_3_out, not_4_out, not_5_out;

  not not_1 (not_1_out, ctrl);
  not not_2 (not_2_out, func[3]);
  not not_3 (not_3_out, func[1]);
  not not_4 (not_4_out, func[0]);
  not not_5 (not_5_out, Be);
  and and_1 (and_1_out, we, not_1_out);
  and and_2 (and_2_out, we, not_2_out);
  and and_3 (and_3_out, we, not_3_out);
  and and_4 (and_4_out, we, not_4_out, not_5_out);
  and and_5 (and_5_out, we, func[0], Be);
  and and_6 (and_6_out, we, func[2]);
  and and_7 (and_7_out, we, func[4]);
  and and_8 (and_8_out, we, func[5]);
  or or_1 (we2, and_1_out, and_2_out, and_3_out, and_4_out, and_5_out, and_6_out, and_7_out, and_8_out);
endmodule

module Func (
  input  a,
  input  b,
  input  c,
  input  d,
  input  e,
  input  f,
  output b_2
);

  wire not_1_out, not_2_out, not_3_out, not_4_out;

  not not_1 (not_1_out, a);
  not not_2 (not_2_out, b);
  not not_3 (not_3_out, d);
  not not_4 (not_4_out, e);
  and and_1 (b_2, not_1_out, not_2_out, c, not_3_out, not_4_out);
endmodule

module hi (
  input  we,
  input  inst,
  input  func,
  output o
);

  wire and_1_out, and_2_out, not_1_out;

  not not_1 (not_1_out, inst);
  and and_1 (and_1_out, we, not_1_out);
  and and_2 (and_2_out, we, func);
  or or_1 (o, and_1_out, and_2_out);
endmodule

module EqB (
  input  [4:0] r,
  input  [4:0] d,
  input  w,
  input  t,
  output out_5
);

  wire and_1_out, and_2_out, not_1_out, not_2_out, not_3_out, not_4_out, not_5_out, not_6_out;
  wire [4:0] xnor_1_out;

  assign xnor_1_out = ~(r ^ d);  // XNOR_Gate xnor_1, 5 bits wide
  not not_1 (not_1_out, d[0]);
  not not_2 (not_2_out, d[1]);
  not not_3 (not_3_out, d[2]);
  not not_4 (not_4_out, d[3]);
  not not_5 (not_5_out, d[4]);
  and and_1 (and_1_out, not_1_out, not_2_out, not_3_out, not_4_out, not_5_out);
  and and_2 (and_2_out, xnor_1_out[0], xnor_1_out[1], xnor_1_out[2], xnor_1_out[3], xnor_1_out[4]);
  not not_6 (not_6_out, and_1_out);
  and and_3 (out_5, not_6_out, and_2_out, w, t);
endmodule

module jaljr (
  input  [5:0] in_1,
  input  in_2,
  output o
);

  wire and_1_out, not_1_out, not_2_out, not_3_out, not_4_out;

  not not_1 (not_1_out, in_1[5]);
  not not_2 (not_2_out, in_1[4]);
  not not_3 (not_3_out, in_1[2]);
  not not_4 (not_4_out, in_1[1]);
  and and_1 (and_1_out, not_1_out, not_2_out, in_1[3], not_3_out, not_4_out);
  and and_2 (o, and_1_out, in_2);
endmodule

module ltz_gez (
  input  [31:0] in_1,
  input  lez,
  output bgez,
  output bltz
);

  wire comparator_1_eq, not_1_out, not_2_out;

  Comparator #(.width(32), .mode("unsigned")) comparator_1 (
    .a(in_1), .b({32{1'b0}}), .eq(comparator_1_eq));  // open: gt, lt
  not not_1 (not_1_out, comparator_1_eq);
  not not_2 (not_2_out, lez);
  and and_1 (bltz, lez, not_1_out);
  or or_1 (bgez, not_2_out, comparator_1_eq);
endmodule

module Jump (
  input  bra,
  input  jal,
  input  [5:0] op,
  output jump
);

  wire and_1_out, and_2_out, and_3_out, and_4_out, not_1_out, not_2_out, not_3_out, not_4_out, not_5_out,
       not_6_out, not_7_out, not_8_out, not_9_out, not_10_out, not_11_out, not_12_out, not_13_out,
       not_14_out, not_15_out;

  not not_1 (not_1_out, op[5]);
  not not_2 (not_2_out, op[4]);
  not not_3 (not_3_out, op[3]);
  not not_4 (not_4_out, op[2]);
  not not_5 (not_5_out, op[0]);
  not not_6 (not_6_out, op[5]);
  not not_7 (not_7_out, op[4]);
  not not_8 (not_8_out, op[3]);
  not not_9 (not_9_out, op[5]);
  not not_10 (not_10_out, op[4]);
  not not_11 (not_11_out, op[3]);
  not not_12 (not_12_out, op[2]);
  not not_13 (not_13_out, op[5]);
  not not_14 (not_14_out, op[4]);
  not not_15 (not_15_out, op[3]);
  and and_1 (and_1_out, not_1_out, not_2_out, not_3_out, not_4_out, not_5_out, jal);
  and and_2 (and_2_out, not_6_out, not_7_out, not_8_out, op[0], bra);
  and and_3 (and_3_out, not_9_out, not_10_out, not_11_out, not_12_out, op[1]);
  and and_4 (and_4_out, not_13_out, not_14_out, not_15_out, op[2], bra);
  or or_1 (jump, and_1_out, and_2_out, and_3_out, and_4_out);
endmodule

module PCsel (
  input  jump,
  input  [5:0] op,
  output [1:0] out_3
);

  wire and_1_out, and_2_out, not_1_out, not_2_out, not_3_out, or_1_out, or_2_out;

  or or_1 (or_1_out, op[0], op[1], op[2]);
  not not_1 (not_1_out, op[2]);
  not not_2 (not_2_out, op[0]);
  not not_3 (not_3_out, op[2]);
  and and_1 (and_1_out, not_1_out, not_2_out);
  and and_2 (and_2_out, not_3_out, op[1]);
  or or_2 (or_2_out, and_1_out, and_2_out);
  and and_3 (out_3[1], jump, or_1_out);
  and and_4 (out_3[0], jump, or_2_out);
endmodule

module ldst (
  input  op5,
  input  a,
  input  b,
  input  c,
  input  d,
  input  op0,
  output ld,
  output st
);

  wire and_1_out, and_2_out, and_3_out, and_4_out, not_1_out, not_2_out, not_3_out, not_4_out, not_5_out,
       not_6_out, not_7_out, not_8_out, not_9_out, not_10_out, not_11_out, not_12_out, not_13_out;

  not not_1 (not_1_out, a);
  not not_2 (not_2_out, b);
  not not_3 (not_3_out, d);
  not not_4 (not_4_out, op0);
  not not_5 (not_5_out, a);
  not not_6 (not_6_out, b);
  not not_7 (not_7_out, c);
  not not_8 (not_8_out, a);
  not not_9 (not_9_out, c);
  not not_10 (not_10_out, d);
  not not_11 (not_11_out, op0);
  not not_12 (not_12_out, a);
  not not_13 (not_13_out, c);
  and and_1 (and_1_out, op5, not_1_out, not_2_out, not_3_out, not_4_out);
  and and_2 (and_2_out, op5, not_5_out, not_6_out, not_7_out, d, op0);
  and and_3 (and_3_out, op5, not_8_out, b, not_9_out, not_10_out, not_11_out);
  and and_4 (and_4_out, op5, not_12_out, b, not_13_out, d, op0);
  or or_1 (ld, and_1_out, and_2_out);
  or or_2 (st, and_3_out, and_4_out);
endmodule

module Stall (
  input  [5:0] dop,
  input  eq,
  output s
);

  wire ld_1_ld;

  ld ld_1 (.op(dop), .ld(ld_1_ld));
  and and_1 (s, eq, ld_1_ld);
endmodule

module ld (
  input  [5:0] op,
  output ld
);

  wire and_1_out, and_2_out, not_1_out, not_2_out, not_3_out, not_4_out, not_5_out, not_6_out, not_7_out;

  not not_1 (not_1_out, op[4]);
  not not_2 (not_2_out, op[3]);
  not not_3 (not_3_out, op[1]);
  not not_4 (not_4_out, op[0]);
  not not_5 (not_5_out, op[4]);
  not not_6 (not_6_out, op[3]);
  not not_7 (not_7_out, op[2]);
  and and_1 (and_1_out, op[5], not_1_out, not_2_out, not_3_out, not_4_out);
  and and_2 (and_2_out, op[5], not_5_out, not_6_out, not_7_out, op[1], op[0]);
  or or_1 (ld, and_1_out, and_2_out);
endmodule

module ctrle (
  input  [5:0] in_1,
  output out_2
);

  wire not_1_out, not_2_out, not_3_out, not_4_out, not_5_out, not_6_out;

  not not_1 (not_1_out, in_1[5]);
  not not_2 (not_2_out, in_1[4]);
  not not_3 (not_3_out, in_1[3]);
  not not_4 (not_4_out, in_1[2]);
  not not_5 (not_5_out, in_1[1]);
  not not_6 (not_6_out, in_1[0]);
  and and_1 (out_2, not_1_out, not_2_out, not_3_out, not_4_out, not_5_out, not_6_out);
endmodule

module sign (
  input  [5:0] in_1,
  output s
);

  wire not_1_out, not_2_out;

  not not_1 (not_1_out, in_1[5]);
  not not_2 (not_2_out, in_1[4]);
  and and_1 (s, not_1_out, not_2_out, in_1[3], in_1[2]);
endmodule

module slt (
  input  [5:0] in_1,
  input  o,
  output out_3
);

  wire and_1_out, not_1_out, not_2_out;

  not not_1 (not_1_out, in_1[4]);
  not not_2 (not_2_out, in_1[2]);
  and and_1 (and_1_out, not_1_out, in_1[3], not_2_out, in_1[1]);
  and and_2 (out_3, and_1_out, o);
endmodule
